# Fritzing sketch tripmaster (saved by Fritzing 0.9.2b)
breadboards: 1

parts:
  Op = Pushbutton [package="[THT]"]
  Neer = Pushbutton [package="[THT]"]
  Reset = Pushbutton [package="[THT]"]
  Ri = Pushbutton [package="[THT]"]
  Menu = Pushbutton [package="[THT]"]
  Part2 = Arduino Leonardo (Rev3b)
  Part3 = Triple Axis Magnetometer - HMC5883 Breakout
  U1 = HALL-EFFECT [package=sc70]
  LCM1602_IIC2 = LCM1602 IIC [part_number="LCM1602 IIC" chip_label="LCM1602 IIC" package="DIP (Dual Inline) [THT]"]
  LCD2 = LCD screen

nets:
  GND: Op.Pin_1, Op.Pin_2, Neer.Pin_1, Neer.Pin_2, Reset.Pin_1, Reset.Pin_2, Ri.Pin_1, Ri.Pin_2, Menu.Pin_1, Menu.Pin_2, Part2.GND, Part3.GND, U1.GND, LCM1602_IIC2.GND
  N1: Op.Pin_3, Op.Pin_4, Part2.D3_PWM/SCL, Part2.SCL, Part3.SDA, LCM1602_IIC2.SCL
  N2: Neer.Pin_3, Neer.Pin_4, Part2.D4/A6
  N3: Reset.Pin_3, Reset.Pin_4, Part2.D5_PWM
  N4: Ri.Pin_3, Ri.Pin_4, Part2.D6_PWM/A7
  N5: Menu.Pin_3, Menu.Pin_4, Part2.D7
  VCC: Part2.5V, Part3.VCC, U1.VCC, LCM1602_IIC2.VCC
  N6: Part2.D8/A8, U1.OUT
  N7: Part2.SDA, Part3.SCL, LCM1602_IIC2.SDA
  VSS: LCM1602_IIC2.VSS, LCD2.VSS
  VDD: LCM1602_IIC2.VDD, LCD2.VDD
  N8: LCM1602_IIC2.V0, LCD2.V0
  N9: LCM1602_IIC2.RS, LCD2.RS
  N10: LCM1602_IIC2.RW, LCD2.R/W
  N11: LCM1602_IIC2.E, LCD2.E
  N12: LCM1602_IIC2.D0, LCD2.DB0
  N13: LCM1602_IIC2.D1, LCD2.DB1
  N14: LCM1602_IIC2.D2, LCD2.DB2
  N15: LCM1602_IIC2.D3, LCD2.DB3
  N16: LCM1602_IIC2.D4, LCD2.DB4
  N17: LCM1602_IIC2.D5, LCD2.DB5
  N18: LCM1602_IIC2.D6, LCD2.DB6
  N19: LCM1602_IIC2.D7, LCD2.DB7
  N20: LCM1602_IIC2.A, LCD2.LED+
  N21: LCM1602_IIC2.K, LCD2.LED-

custom parts:
  LCM1602 IIC: I2C-Module to use a 1602 or 2004 LCD on with the wire.h libory Serial LCD Modul
